// Logisim project 1_bit_register.circ as structural Verilog: 1 circuit, main circuit main
module main (
  input  Load,
  input  Clock,
  input  in_3,
  input  D1
);

  wire and_1_out, and_2_out, not_1_out, or_1_out;

  not not_1 (not_1_out, Load);
  and and_1 (and_1_out, in_3, not_1_out);
  and and_2 (and_2_out, Load, D1);
  or or_1 (or_1_out, and_1_out, and_2_out);
  D_Flip_Flop d_ff_1 (.clk(Clock), .D(or_1_out), .Q(in_3));  // open: Qn, preset, en, reset
endmodule
