// Logisim project Processor.circ as structural Verilog: 13 circuits, main circuit main
module main (
);

  wire alu_8bit_1_set_out, alu_8bit_1_zero, and_1_out, control_1_branch, control_1_clk, control_1_jump,
       control_1_memwrite, control_1_regwrite;
  wire [1:0] control_1_alusrc, control_1_memtoreg;
  wire [3:0] control_1_aluop;
  wire [5:0] rom_1_op;
  wire [7:0] alu_8bit_1_result, bit_extender_1_out, bit_extender_2_out, multiplexer_1_out, multiplexer_2_out,
       multiplexer_3_out, multiplexer_4_out, n8_bit_addr_1_sum, n8_bit_addr_2_sum, PC_data_out, ram_1_data,
       registerfile_1_data_a, registerfile_1_data_b, shifter_1_out;
  wire [7:6] rom_1_op_2;

  _8_Bit_Register PC (
    .CLK(control_1_clk), .Enb(1'b1), .Load(1'b1), .Data_in(multiplexer_1_out), .Data_out(PC_data_out));
  _8_bit_addr u_8_bit_addr_1 (.sum(n8_bit_addr_1_sum), .A(PC_data_out), .B(8'h1));
  assign bit_extender_1_out = {{2{1'b0}}, rom_1_op};  // Bit_Extender bit_extender_1
  // Probe on {rom_1_op_2, rom_1_op}
  ROM rom_1 (.PC(PC_data_out), .OP({rom_1_op_2, rom_1_op}));
  Multiplexer #(.width(8), .enable("false")) multiplexer_1 (
    .in0(multiplexer_3_out), .in1(shifter_1_out), .out(multiplexer_1_out), .sel(control_1_jump));
  Control control_1 (
    .OPcode({rom_1_op_2, rom_1_op}), .Jump(control_1_jump), .Branch(control_1_branch),
    .MemToReg(control_1_memtoreg), .MemWrite(control_1_memwrite), .ALUsrc(control_1_alusrc),
    .RegWrite(control_1_regwrite), .CLK(control_1_clk), .ALUOP(control_1_aluop));
  Shifter shifter_1 (.in(bit_extender_1_out), .\dist (3'b010), .out(shifter_1_out));
  _8_bit_addr u_8_bit_addr_2 (.sum(n8_bit_addr_2_sum), .A(n8_bit_addr_1_sum), .B(bit_extender_1_out));
  RegisterFile registerfile_1 (
    .InputA(rom_1_op[3:2]), .InputB(rom_1_op[1:0]), .WriteIn(multiplexer_4_out),
    .Data_A(registerfile_1_data_a), .Data_B(registerfile_1_data_b), .WriteFlag(control_1_regwrite),
    .CLK(control_1_clk));
  assign bit_extender_2_out = {{6{1'b0}}, rom_1_op[1:0]};  // Bit_Extender bit_extender_2
  and and_1 (and_1_out, control_1_branch, alu_8bit_1_zero);
  ALU_8bit alu_8bit_1 (
    .A(registerfile_1_data_a), .set_in(alu_8bit_1_set_out), .B(multiplexer_2_out),
    .set_out(alu_8bit_1_set_out), .Zero(alu_8bit_1_zero), .Result(alu_8bit_1_result),
    .AInv_Binv_OP(control_1_aluop));  // open: Overflow, C_out
  Multiplexer #(.select(2), .width(8), .enable("false")) multiplexer_2 (
    .in0(registerfile_1_data_b), .in1({8{1'b0}}), .in2(bit_extender_2_out), .in3({8{1'b0}}),
    .out(multiplexer_2_out), .sel(control_1_alusrc));
  Multiplexer #(.width(8), .enable("false")) multiplexer_3 (
    .in0(n8_bit_addr_1_sum), .in1(n8_bit_addr_2_sum), .out(multiplexer_3_out), .sel(and_1_out));
  RAM ram_1 (
    .Address(alu_8bit_1_result), .Data_in(registerfile_1_data_b), .CLK(control_1_clk), .Data(ram_1_data),
    .store(control_1_memwrite));
  Multiplexer #(.select(2), .width(8), .enable("false")) multiplexer_4 (
    .in0(alu_8bit_1_result), .in1(ram_1_data), .in2(bit_extender_2_out), .out(multiplexer_4_out),
    .sel(control_1_memtoreg));  // open: in3
endmodule

module _1_bit_register (
  input  Clk,
  input  Load,
  input  Enb,
  input  Data,
  output D_Out
);

  wire and_1_out, and_2_out, d_ff_1_q, not_1_out, or_1_out;

  not not_1 (not_1_out, Load);
  and and_1 (and_1_out, d_ff_1_q, not_1_out);
  and and_2 (and_2_out, Load, Data);
  or or_1 (or_1_out, and_1_out, and_2_out);
  D_Flip_Flop d_ff_1 (.clk(Clk), .D(or_1_out), .Q(d_ff_1_q));  // open: Qn, preset, en, reset
  and and_3 (D_Out, d_ff_1_q, Enb);
endmodule

module Clock (
  input  Clk,
  input  R,
  input  Manuel,
  input  Halt,
  output Clk_Out
);

  wire and_1_out, and_2_out, d_ff_1_q, nor_1_out, nor_2_out, not_1_out, or_1_out, or_2_out;

  not not_1 (not_1_out, R);
  nor nor_1 (nor_1_out, R, nor_2_out);
  nor nor_2 (nor_2_out, nor_1_out, not_1_out);
  or or_1 (or_1_out, Halt, d_ff_1_q);
  D_Flip_Flop #(.trigger("high")) d_ff_1 (.clk(Halt), .D(or_1_out), .Q(d_ff_1_q));  // open: Qn, preset, en, reset
  and and_1 (and_1_out, Clk, nor_1_out);
  and and_2 (and_2_out, Manuel, nor_2_out);
  or or_2 (or_2_out, and_1_out, and_2_out);
  or or_3 (Clk_Out, or_2_out, d_ff_1_q);
endmodule

module _8_Bit_Register (
  input  CLK,
  input  Enb,
  input  Load,
  input  [7:0] Data_in,
  output [7:0] Data_out
);

  _1_bit_register u_1_bit_register_1 (.Clk(CLK), .Load(Load), .D_Out(Data_out[0]), .Data(Data_in[0]), .Enb(Enb));
  _1_bit_register u_1_bit_register_2 (.Clk(CLK), .Load(Load), .D_Out(Data_out[1]), .Data(Data_in[1]), .Enb(Enb));
  _1_bit_register u_1_bit_register_3 (.Clk(CLK), .Load(Load), .D_Out(Data_out[2]), .Data(Data_in[2]), .Enb(Enb));
  _1_bit_register u_1_bit_register_4 (.Clk(CLK), .Load(Load), .D_Out(Data_out[3]), .Data(Data_in[3]), .Enb(Enb));
  _1_bit_register u_1_bit_register_5 (.Clk(CLK), .Load(Load), .D_Out(Data_out[4]), .Data(Data_in[4]), .Enb(Enb));
  _1_bit_register u_1_bit_register_6 (.Clk(CLK), .Load(Load), .D_Out(Data_out[5]), .Data(Data_in[5]), .Enb(Enb));
  _1_bit_register u_1_bit_register_7 (.Clk(CLK), .Load(Load), .D_Out(Data_out[6]), .Data(Data_in[6]), .Enb(Enb));
  _1_bit_register u_1_bit_register_8 (.Clk(CLK), .Load(Load), .D_Out(Data_out[7]), .Data(Data_in[7]), .Enb(Enb));
endmodule

module _1_bit_addr (
  input  C_in,
  input  A,
  input  B,
  output Sum,
  output C_out
);

  wire and_1_out, and_2_out, xor_1_out;

  xor xor_1 (xor_1_out, B, A);
  and and_1 (and_1_out, A, B);
  xor xor_2 (Sum, xor_1_out, C_in);
  and and_2 (and_2_out, xor_1_out, C_in);
  or or_1 (C_out, and_2_out, and_1_out);
endmodule

module _8_bit_addr (
  input  [7:0] A,
  input  [7:0] B,
  output [7:0] sum
);

  wire n1_bit_addr_1_c_out, n1_bit_addr_2_c_out, n1_bit_addr_3_c_out, n1_bit_addr_4_c_out,
       n1_bit_addr_5_c_out, n1_bit_addr_6_c_out, n1_bit_addr_7_c_out;

  _1_bit_addr u_1_bit_addr_1 (.Sum(sum[0]), .C_out(n1_bit_addr_1_c_out), .C_in(1'b0), .A(B[0]), .B(A[0]));
  _1_bit_addr u_1_bit_addr_2 (
    .Sum(sum[1]), .C_out(n1_bit_addr_2_c_out), .C_in(n1_bit_addr_1_c_out), .A(B[1]), .B(A[1]));
  _1_bit_addr u_1_bit_addr_3 (
    .Sum(sum[2]), .C_out(n1_bit_addr_3_c_out), .C_in(n1_bit_addr_2_c_out), .A(B[2]), .B(A[2]));
  _1_bit_addr u_1_bit_addr_4 (
    .Sum(sum[3]), .C_out(n1_bit_addr_4_c_out), .C_in(n1_bit_addr_3_c_out), .A(B[3]), .B(A[3]));
  _1_bit_addr u_1_bit_addr_5 (
    .Sum(sum[4]), .C_out(n1_bit_addr_5_c_out), .C_in(n1_bit_addr_4_c_out), .A(B[4]), .B(A[4]));
  _1_bit_addr u_1_bit_addr_6 (
    .Sum(sum[5]), .C_out(n1_bit_addr_6_c_out), .C_in(n1_bit_addr_5_c_out), .A(B[5]), .B(A[5]));
  _1_bit_addr u_1_bit_addr_7 (
    .Sum(sum[6]), .C_out(n1_bit_addr_7_c_out), .C_in(n1_bit_addr_6_c_out), .A(B[6]), .B(A[6]));
  _1_bit_addr u_1_bit_addr_8 (.Sum(sum[7]), .C_in(n1_bit_addr_7_c_out), .A(B[7]), .B(A[7]));  // open: C_out
endmodule

module ALU_1_bit (
  input  c_in,
  input  a_0,
  input  A_inv,
  input  [1:0] Opt,
  input  b_0,
  input  b_inv,
  input  Less,
  output Result,
  output C_out
);

  wire and_1_out, n1_bit_addr_1_sum, or_1_out, xor_1_out, xor_2_out;

  xor xor_1 (xor_1_out, a_0, A_inv);
  xor xor_2 (xor_2_out, b_0, b_inv);
  _1_bit_addr u_1_bit_addr_1 (.Sum(n1_bit_addr_1_sum), .C_out(C_out), .C_in(c_in), .A(xor_2_out), .B(xor_1_out));
  and and_1 (and_1_out, xor_1_out, xor_2_out);
  or or_1 (or_1_out, xor_1_out, xor_2_out);
  Multiplexer #(.select(2), .enable("false")) multiplexer_1 (
    .in0(and_1_out), .in1(or_1_out), .in2(n1_bit_addr_1_sum), .in3(Less), .out(Result), .sel(Opt));
endmodule

module ALU_8bit (
  input  [3:0] AInv_Binv_OP,
  input  [7:0] A,
  input  set_in,
  input  [7:0] B,
  output Zero,
  output [7:0] Result,
  output Overflow,
  output set_out,
  output C_out
);

  wire alu_1_bit_1_c_out, alu_1_bit_2_c_out, alu_1_bit_3_c_out, alu_1_bit_4_c_out, alu_1_bit_5_c_out,
       alu_1_bit_6_c_out, alu_1_bit_7_c_out, or_1_out, xor_1_out;

  xor xor_1 (xor_1_out, AInv_Binv_OP[2], AInv_Binv_OP[3]);
  ALU_1_bit alu_1_bit_1 (
    .a_0(A[0]), .A_inv(AInv_Binv_OP[3]), .b_0(B[0]), .b_inv(AInv_Binv_OP[2]), .Less(set_in),
    .Result(Result[0]), .c_in(xor_1_out), .Opt(AInv_Binv_OP[1:0]), .C_out(alu_1_bit_1_c_out));
  ALU_1_bit alu_1_bit_2 (
    .a_0(A[1]), .A_inv(AInv_Binv_OP[3]), .b_0(B[1]), .b_inv(AInv_Binv_OP[2]), .Less(1'b0),
    .Result(Result[1]), .c_in(alu_1_bit_1_c_out), .Opt(AInv_Binv_OP[1:0]), .C_out(alu_1_bit_2_c_out));
  ALU_1_bit alu_1_bit_3 (
    .a_0(A[2]), .A_inv(AInv_Binv_OP[3]), .b_0(B[2]), .b_inv(AInv_Binv_OP[2]), .Less(1'b0),
    .Result(Result[2]), .c_in(alu_1_bit_2_c_out), .Opt(AInv_Binv_OP[1:0]), .C_out(alu_1_bit_3_c_out));
  ALU_1_bit alu_1_bit_4 (
    .a_0(A[3]), .A_inv(AInv_Binv_OP[3]), .b_0(B[3]), .b_inv(AInv_Binv_OP[2]), .Less(1'b0),
    .Result(Result[3]), .c_in(alu_1_bit_3_c_out), .Opt(AInv_Binv_OP[1:0]), .C_out(alu_1_bit_4_c_out));
  ALU_1_bit alu_1_bit_5 (
    .a_0(A[4]), .A_inv(AInv_Binv_OP[3]), .b_0(B[4]), .b_inv(AInv_Binv_OP[2]), .Less(1'b0),
    .Result(Result[4]), .c_in(alu_1_bit_4_c_out), .Opt(AInv_Binv_OP[1:0]), .C_out(alu_1_bit_5_c_out));
  ALU_1_bit alu_1_bit_6 (
    .a_0(A[5]), .A_inv(AInv_Binv_OP[3]), .b_0(B[5]), .b_inv(AInv_Binv_OP[2]), .Less(1'b0),
    .Result(Result[5]), .c_in(alu_1_bit_5_c_out), .Opt(AInv_Binv_OP[1:0]), .C_out(alu_1_bit_6_c_out));
  ALU_1_bit alu_1_bit_7 (
    .a_0(A[6]), .A_inv(AInv_Binv_OP[3]), .b_0(B[6]), .b_inv(AInv_Binv_OP[2]), .Less(1'b0),
    .Result(Result[6]), .c_in(alu_1_bit_6_c_out), .Opt(AInv_Binv_OP[1:0]), .C_out(alu_1_bit_7_c_out));
  ALU_1_bit_set_overflow alu_1_bit_set_overflow_1 (
    .a_0(A[7]), .A_inv(AInv_Binv_OP[3]), .b_0(B[7]), .b_inv(AInv_Binv_OP[2]), .Less(1'b0),
    .Result(Result[7]), .c_in(alu_1_bit_7_c_out), .Opt(AInv_Binv_OP[1:0]), .C_out(C_out),
    .overflow(Overflow), .set(set_out));
  or or_1 (or_1_out, Result[0], Result[1], Result[2], Result[3], Result[4], Result[5], Result[6], Result[7]);
  not not_1 (Zero, or_1_out);
endmodule

module ALU_1_bit_set_overflow (
  input  c_in,
  input  a_0,
  input  A_inv,
  input  [1:0] Opt,
  input  b_0,
  input  b_inv,
  input  Less,
  output Result,
  output C_out,
  output overflow,
  output set
);

  wire and_1_out, or_1_out, xor_1_out, xor_2_out;

  xor xor_1 (xor_1_out, a_0, A_inv);
  xor xor_2 (xor_2_out, b_0, b_inv);
  _1_bit_addr u_1_bit_addr_1 (.Sum(set), .C_out(C_out), .C_in(c_in), .A(xor_2_out), .B(xor_1_out));
  and and_1 (and_1_out, xor_1_out, xor_2_out);
  or or_1 (or_1_out, xor_1_out, xor_2_out);
  Multiplexer #(.select(2), .enable("false")) multiplexer_1 (
    .in0(and_1_out), .in1(or_1_out), .in2(set), .in3(Less), .out(Result), .sel(Opt));

  assign overflow = C_out;
endmodule

module RegisterFile (
  input  WriteFlag,
  input  [1:0] InputA,
  input  [1:0] InputB,
  input  [7:0] WriteIn,
  input  CLK,
  output [7:0] Data_A,
  output [7:0] Data_B
);

  wire decoder_1_out0, decoder_1_out1, decoder_1_out2, decoder_1_out3;
  wire [7:0] multiplexer_1_out, n8_bit_register_1_data_out, n8_bit_register_2_data_out,
       n8_bit_register_3_data_out, n8_bit_register_4_data_out;

  Decoder #(.select(2), .disabled(0)) decoder_1 (
    .out0(decoder_1_out0), .out1(decoder_1_out1), .out2(decoder_1_out2), .out3(decoder_1_out3), .sel(InputA),
    .en(WriteFlag));
  Multiplexer #(.width(8), .enable("false")) multiplexer_1 (
    .in0({8{1'b0}}), .in1(WriteIn), .out(multiplexer_1_out), .sel(WriteFlag));
  _8_Bit_Register u_8_bit_register_1 (
    .CLK(CLK), .Enb(1'b1), .Load(decoder_1_out0), .Data_in(multiplexer_1_out),
    .Data_out(n8_bit_register_1_data_out));
  _8_Bit_Register u_8_bit_register_2 (
    .CLK(CLK), .Enb(1'b1), .Load(decoder_1_out1), .Data_in(multiplexer_1_out),
    .Data_out(n8_bit_register_2_data_out));
  _8_Bit_Register u_8_bit_register_3 (
    .CLK(CLK), .Enb(1'b1), .Load(decoder_1_out2), .Data_in(multiplexer_1_out),
    .Data_out(n8_bit_register_3_data_out));
  _8_Bit_Register u_8_bit_register_4 (
    .CLK(CLK), .Enb(1'b1), .Load(decoder_1_out3), .Data_in(multiplexer_1_out),
    .Data_out(n8_bit_register_4_data_out));
  Multiplexer #(.select(2), .width(8), .enable("false")) multiplexer_2 (
    .in0(n8_bit_register_1_data_out), .in1(n8_bit_register_2_data_out), .in2(n8_bit_register_3_data_out),
    .in3(n8_bit_register_4_data_out), .out(Data_A), .sel(InputA));
  Multiplexer #(.select(2), .width(8), .enable("false")) multiplexer_3 (
    .in0(n8_bit_register_1_data_out), .in1(n8_bit_register_2_data_out), .in2(n8_bit_register_3_data_out),
    .in3(n8_bit_register_4_data_out), .out(Data_B), .sel(InputB));
endmodule

module RAM (
  input  [7:0] Address,
  input  [7:0] Data_in,
  input  CLK,
  input  store,
  output [7:0] Data
);

  RAM_part #(.bus("separate")) ram_1 (
    .addr(Address), .din(Data_in), .data(Data), .str(store), .sel(1'b1), .clk(CLK), .ld(1'b1));  // open: clr
endmodule

module Control (
  input  [7:0] OPcode,
  output Jump,
  output Branch,
  output [1:0] MemToReg,
  output MemWrite,
  output [1:0] ALUsrc,
  output RegWrite,
  output [3:0] ALUOP,
  output CLK
);

  Clock_part clock_1 (.out(CLK));
  ROM_part #(.addrWidth(4), .dataWidth(12)) rom_1 (
    .addr(OPcode[7:4]), .data({Jump, Branch, MemToReg, MemWrite, ALUsrc, RegWrite, ALUOP}), .sel(1'b1));

  // Notes on the sheet:
  //   contents of rom_1 (hex, n*v repeats v):
  //   12 10 11 16 13 406 0 0 a2 132 250 0 4*800
endmodule

module ROM (
  input  [7:0] PC,
  output [7:0] OP
);

  ROM_part rom_1 (.addr(PC), .data(OP), .sel(1'b1));

  // Notes on the sheet:
  //   contents of rom_1 (hex, n*v repeats v):
  //   a1 a5 88 c1 c 1 a4 27 ad b 88 ac c1
endmodule
